# Fritzing sketch potentiometer (saved by Fritzing 0.9.3b)

parts:
  U1 = POT [package=pot_mammoth]
  Part1 = Arduino Uno (Rev3)

nets:
  N1: U1.S, Part1.GND
  N2: U1.A, Part1.A0
  N3: U1.E, Part1.5V
