# Fritzing sketch potentiometer_led (saved by Fritzing 0.9.3b)
breadboards: 1

parts:
  U1 = POT [package=pot_mammoth]
  Part1 = Arduino Uno (Rev3)
  LED1 = LED - 3mm [color="Red (633nm)" package="3 mm [THT]"]
  R1 = Resistor [tolerance=±5% resistance=220 package="1206 [SMD]"]

nets:
  N1: U1.S, Part1.GND, LED1.cathode
  N2: U1.A, Part1.A0
  N3: U1.E, Part1.5V
  N4: Part1.D11_PWM/MOSI, R1.Pin_1
  N5: LED1.anode, R1.Pin_0
