# Fritzing sketch capacitive_sensing (saved by Fritzing 0.9.3b)

parts:
  Part1 = Arduino Uno (Rev3)
  1MOhm = Resistor [tolerance=±5% resistance=1M package="2010 [SMD]"]

nets:
  N1: Part1.A0, 1MOhm.Pin_0
  N2: Part1.GND, 1MOhm.Pin_1

notes:
  hier berühren
