# Fritzing sketch hotwire_3 (saved by Fritzing 0.9.3b)
breadboards: 1

parts:
  Part1 = Arduino Uno (Rev3) - ICSP
  LED1 = smd LED [color="Red (633nm)" package="0805 [SMD]"]
  R2 = Resistor [tolerance=±5% resistance=10k package="1206 [SMD]"]
  LED2 = smd LED [color="Yellow (595nm)" package="0805 [SMD]"]
  LED3 = smd LED [color="Green (565nm)" package="0805 [SMD]"]
  R3 = Resistor [tolerance=±5% resistance=220 package="1206 [SMD]"]
  R4 = Resistor [tolerance=±5% resistance=220 package="1206 [SMD]"]
  R5 = Resistor [tolerance=±5% resistance=220 package="1206 [SMD]"]
  SPKR1 = Loudspeaker
  R6 = Resistor [tolerance=±5% resistance=1k package="1206 [SMD]"]

nets:
  N1: Part1.D9_PWM, R5.Pin_1
  N2: Part1.D10_PWM/SS, R4.Pin_1
  N3: Part1.D11_PWM/MOSI, R3.Pin_1
  N4: Part1.GND, LED1.cathode, R2.Pin_1, LED2.cathode, LED3.cathode, SPKR1.pin1
  N5: Part1.D6_PWM, R6.Pin_0
  N6: Part1.D7, R2.Pin_0
  N7: LED1.anode, R3.Pin_0
  N8: LED2.anode, R4.Pin_0
  N9: LED3.anode, R5.Pin_0
  N10: SPKR1.pin2, R6.Pin_1
