# Fritzing sketch arduino_pov_8_led (saved by Fritzing 0.9.4)
breadboards: 1

parts:
  Part1 = Arduino Uno (Rev3)
  R1 = Resistor [tolerance=±5% resistance=220 package="0603 [SMD]"]
  LED1 = smd LED [color="Red (633nm)" package="0805 [SMD]"]
  R2 = Resistor [tolerance=±5% resistance=220 package="0603 [SMD]"]
  LED2 = smd LED [color="Red (633nm)" package="0805 [SMD]"]
  R3 = Resistor [tolerance=±5% resistance=220 package="0603 [SMD]"]
  LED3 = smd LED [color="Red (633nm)" package="0805 [SMD]"]
  R4 = Resistor [tolerance=±5% resistance=220 package="0603 [SMD]"]
  LED4 = smd LED [color="Red (633nm)" package="0805 [SMD]"]
  R5 = Resistor [tolerance=±5% resistance=220 package="0603 [SMD]"]
  LED5 = smd LED [color="Red (633nm)" package="0805 [SMD]"]
  R6 = Resistor [tolerance=±5% resistance=220 package="0603 [SMD]"]
  LED6 = smd LED [color="Red (633nm)" package="0805 [SMD]"]
  R7 = Resistor [tolerance=±5% resistance=220 package="0603 [SMD]"]
  LED7 = smd LED [color="Red (633nm)" package="0805 [SMD]"]
  R8 = Resistor [tolerance=±5% resistance=220 package="0603 [SMD]"]
  LED8 = smd LED [color="Red (633nm)" package="0805 [SMD]"]

nets:
  N1: Part1.D8, R2.Pin_1
  N2: Part1.D9_PWM, R1.Pin_1
  N3: Part1.GND, LED1.cathode, LED2.cathode, LED3.cathode, LED4.cathode, LED5.cathode, LED6.cathode, LED7.cathode, LED8.cathode
  N4: Part1.D2, R8.Pin_1
  N5: Part1.D3_PWM, R7.Pin_1
  N6: Part1.D4, R6.Pin_1
  N7: Part1.D5_PWM, R5.Pin_1
  N8: Part1.D6_PWM, R4.Pin_1
  N9: Part1.D7, R3.Pin_1
  N10: R1.Pin_0, LED1.anode
  N11: R2.Pin_0, LED2.anode
  N12: R3.Pin_0, LED3.anode
  N13: R4.Pin_0, LED4.anode
  N14: R5.Pin_0, LED5.anode
  N15: R6.Pin_0, LED6.anode
  N16: R7.Pin_0, LED7.anode
  N17: R8.Pin_0, LED8.anode
